# Fritzing sketch Anti Sleep Alarm (saved by Fritzing 0.9.3b)
circuit board: 8.46667cm x 5.91131cm

parts:
  Part1 = Arduino Micro (Rev3)
  Eye_blink_sensor = Infrared Proximity Sensor
  Buzzer = Buzzer 12mm [part_number=COM-07950 package=buzzer-12mm-ns]
  Motor = Basic Servo

nets:
  GND: Part1.GND, Eye_blink_sensor.GND, Buzzer.2, Motor.gnd
  N1: Part1.D2/SDA, Eye_blink_sensor.Vout
  N2: Part1.D8_PWM/A8, Motor.pulse
  N3: Part1.D9_PWM/A9, Buzzer.1
  VCC: Part1.5V, Eye_blink_sensor.Vcc, Motor.vcc

custom parts:
  Buzzer 12mm: Buzzer 12mm Spark Fun Electronics SKU : Comp-Buzzer Through hole This is a small 12mm round speaker that operates around the audible 2kHz range. You can use these speakers to create simple music or user interfaces. This is not a true piezoelectric speaker but behaves similarly. Instead of a piezoelectric crystal that vibrates with an electric current, this tiny speaker uses an electromagnet to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

// code stored in the sketch: V1 Code Anti sleep alarm.ino
// Anti sleep alarm for drivers
const int sensorPin = 2;     // Pin connected to the IR sensor (or eye detection sensor)
const int motorPin = 8;      // Pin connected to the motor
const int buzzerPin = 9;     // Pin connected to the buzzer
long time;  // Variable to store time
void setup() {
  pinMode(motorPin, OUTPUT);   // Set motorPin as an OUTPUT
    pinMode(buzzerPin, OUTPUT);  // Set buzzerPin as an OUTPUT
    pinMode(sensorPin, INPUT);   // Set sensorPin as an INPUT
    digitalWrite(motorPin, HIGH); // Turn on the motor initially
}
void loop() {
    // Check if the IR sensor (sensorPin) is triggered (LOW means it's triggered)
  if (!digitalRead(sensorPin)) {
        time = millis();  // Record the current time
        // Keep checking if the IR sensor is still triggered
    while (!digitalRead(sensorPin)) {
      // When the IR sensor is triggered, turn off the buzzer and turn on the motor and wait for 1 second
      digitalWrite(buzzerPin, LOW);
      digitalWrite(motorPin, HIGH);
      delay(1000);
    }
  } else {
    // If the IR sensor is not triggered (eyes open)


    // Check the time elapsed since the sensor was last triggered
    if (TimeDelay() >= 3) {
      digitalWrite(buzzerPin, HIGH);  // If 3 seconds have passed, turn on the buzzer
    }
    if (TimeDelay() >= 4) {
      digitalWrite(motorPin, LOW);   // If 4 seconds have passed, turn off the motor
    }
  }
}


int TimeDelay() {
  long t = millis() - time;  // Calculate the time elapsed since the IR sensor was triggered
  t = t / 1000;  // Convert milliseconds to seconds
  return t;  // Return the elapsed time in seconds
}
