# Fritzing sketch Not Gate (saved by Fritzing 0.9.3b)
circuit board: 6.0054cm x 3.79146cm

parts:
  Q1 = NPN-Transistor [package="TO92 [THT]"]
  R2 = Resistor [tolerance=±5% resistance=220 package=THT]
  R3 = Resistor [tolerance=±5% resistance=1k package=THT]
  R4 = Resistor [tolerance=±5% resistance=10k package=THT]
  S1 = Pushbutton [package="[THT]"]
  LED1 = LED - 5mm [color="Red (633nm)" package="5 mm [THT]"]
  R5 = Resistor [tolerance=±5% resistance=1k package=THT]
  LED2 = LED - 5mm [color="Red (633nm)" package="5 mm [THT]"]
  U1 = Voltage Regulator - 5V [package="DPak [SMD]"]
  BAT1 = BC9VPC [package=bc9vpc]

nets:
  N1: Q1.E, R4.Pin_1, R5.Pin_0, LED2.cathode, U1.GND, BAT1.V-
  N2: Q1.B, R2.Pin_1, R4.Pin_0
  N3: Q1.C, R3.Pin_0, LED1.anode
  N4: R2.Pin_0, S1.Pin_3, S1.Pin_4, LED2.anode
  N5: R3.Pin_1, S1.Pin_1, S1.Pin_2, U1.output_voltage
  N6: LED1.cathode, R5.Pin_1
  N7: U1.input_voltage, BAT1.V+
