# Fritzing sketch NOT Gate Basic(BC547) (saved by Fritzing 0.9.3b)
circuit board: 8.46667cm x 5.64444cm

parts:
  Resistor = Resistor [tolerance=±5% resistance=1k power=1W package=THT]
  9V = BC9VPC [package=bc9vpc]
  S1 = Round Pushbutton
  OUTPUT_LED = LED - 3mm [color="Red (633nm)" package="3 mm [THT]"]
  Q2 = NPN-Transistor [package="TO92 [THT]"]

nets:
  N1: Resistor.Pin_0, 9V.V+, S1.leg1
  N2: Resistor.Pin_1, OUTPUT_LED.anode, Q2.C
  N3: 9V.V-, OUTPUT_LED.cathode, Q2.E
  N4: S1.leg0, Q2.B

custom parts:
  NPN-Transistor: A standard NPN-transistor
