# Fritzing sketch OR Gate Basic(BC547) (saved by Fritzing 0.9.3b)
circuit board: 10cm x 6cm

parts:
  9V1 = BC9VPC [package=bc9vpc]
  Resistor2 = Resistor [tolerance=±5% resistance=10k power=1W package=THT]
  S5 = Round Pushbutton
  OUTPUT_LED2 = LED - 3mm [color="Red (633nm)" package="3 mm [THT]"]
  S4 = Round Pushbutton
  Q6 = NPN-Transistor [package="TO92 [THT]"]
  Q7 = NPN-Transistor [package="TO92 [THT]"]

nets:
  N1: 9V1.V+, S5.leg1, S4.leg1, Q6.C, Q7.C
  N2: 9V1.V-, Resistor2.Pin_1, OUTPUT_LED2.cathode
  N3: Resistor2.Pin_0, OUTPUT_LED2.anode, Q6.E, Q7.E
  N4: S5.leg0, Q6.B
  N5: S4.leg0, Q7.B

custom parts:
  NPN-Transistor: A standard NPN-transistor
