# Fritzing sketch Fire Detection Exhaust System (saved by Fritzing 0.9.3b)
circuit board: 22.5438cm x 8.82493cm
breadboards: 1

parts:
  Part1 = Arduino Uno (Rev3) - ICSP
  Mod1 = KY-019 5V Relay Module [package="Breakout board"]
  M2 = DC Motor
  J1 = Power Jack [package=power_jack_pth]

nets:
  GND: Part1.GND, Mod1.-, M2.pin_1, J1.GND, J1.GNDBREAK
  N1: Part1.D5_PWM, Mod1.S
  N2: Part1.VIN, Mod1.Common, J1.PWR
  N3: Mod1.NO, M2.pin_2

custom parts:
  KY-019 5V Relay Module: KY-019 5V Relay module, used to control AC circuits. (Special thanks to vanepp for fixing the PCB holes and other errors)

// code stored in the sketch: Fire Detection.ino
void setup() {
  Serial.begin(9600);
  pinMode(3, INPUT);
  pinMode(4, OUTPUT);
  pinMode(5, OUTPUT);
}


void loop() {
  int F = digitalRead(3);
  if(F==0)
  {
    digitalWrite(4, LOW);
    digitalWrite(5, HIGH);
  }
  else{
    digitalWrite(4, HIGH);
    digitalWrite(5, LOW);
  }
  Serial.println(F);
  delay(500);
}
